// Logisim project control-logic.circ as structural Verilog: 1 circuit, main circuit control_logic
module control_logic (
  input  [31:0] Instruction,
  input  BrEq,
  input  BrLt,
  output PCSel,
  output RegWEn,
  output [2:0] ImmSel,
  output BrUn,
  output ASel,
  output BSel,
  output [3:0] ALUSel,
  output MemWEn,
  output [1:0] WBSel
);

  wire comparator_8_eq, comparator_9_eq, comparator_10_eq, comparator_11_eq, comparator_12_eq,
       comparator_13_eq, comparator_14_eq, comparator_15_eq, comparator_16_eq, comparator_17_eq,
       comparator_18_eq, comparator_19_eq, comparator_20_eq, comparator_21_eq, is_add, is_add0, is_addi,
       is_and, is_and0, is_andi, is_itype, is_mul, is_mul0, is_mulh, is_mulh0, is_mulhu, is_mulhu0, is_or,
       is_or0, is_ori, is_rtype, is_sll, is_sll0, is_slli, is_slt, is_slt0, is_slti, is_sra, is_sra0,
       is_srai, is_srl, is_srl0, is_srli, is_sub, is_sub0, is_xor, is_xor0, is_xori;
  wire [5:0] ROMInput;
  wire [15:14] rom_1_data;

  Comparator #(.width(7)) comparator_1 (.a(Instruction[6:0]), .b(7'b0010011), .eq(is_itype));  // open: gt, lt
  Comparator #(.width(7)) comparator_2 (.a(Instruction[6:0]), .b(7'b0110011), .eq(is_rtype));  // open: gt, lt
  Comparator #(.width(3)) comparator_3 (.a(Instruction[14:12]), .b(3'b000), .eq(is_add));  // open: gt, lt
  Comparator #(.width(3)) comparator_4 (.a(Instruction[14:12]), .b(3'b111), .eq(is_and));  // open: gt, lt
  Comparator #(.width(3)) comparator_5 (.a(Instruction[14:12]), .b(3'b110), .eq(is_or));  // open: gt, lt
  Comparator #(.width(3)) comparator_6 (.a(Instruction[14:12]), .b(3'b100), .eq(is_xor));  // open: gt, lt
  Comparator #(.width(3)) comparator_7 (.a(Instruction[14:12]), .b(3'b010), .eq(is_slt));  // open: gt, lt
  Comparator #(.width(3)) comparator_8 (.a(Instruction[14:12]), .b(3'b001), .eq(comparator_8_eq));  // open: gt, lt
  Comparator #(.width(7)) comparator_9 (.a(Instruction[31:25]), .b({7{1'b0}}), .eq(comparator_9_eq));  // open: gt, lt
  Comparator #(.width(3)) comparator_10 (.a(Instruction[14:12]), .b(3'b101), .eq(comparator_10_eq));  // open: gt, lt
  Comparator #(.width(7)) comparator_11 (.a(Instruction[31:25]), .b({7{1'b0}}), .eq(comparator_11_eq));  // open: gt, lt
  Comparator #(.width(3)) comparator_12 (.a(Instruction[14:12]), .b(3'b101), .eq(comparator_12_eq));  // open: gt, lt
  Comparator #(.width(7)) comparator_13 (
    .a(Instruction[31:25]), .b(7'b0100000), .eq(comparator_13_eq));  // open: gt, lt
  Comparator #(.width(3)) comparator_14 (.a(Instruction[14:12]), .b(3'b000), .eq(comparator_14_eq));  // open: gt, lt
  Comparator #(.width(7)) comparator_15 (
    .a(Instruction[31:25]), .b(7'b0000001), .eq(comparator_15_eq));  // open: gt, lt
  Comparator #(.width(3)) comparator_16 (.a(Instruction[14:12]), .b(3'b001), .eq(comparator_16_eq));  // open: gt, lt
  Comparator #(.width(7)) comparator_17 (
    .a(Instruction[31:25]), .b(7'b0000001), .eq(comparator_17_eq));  // open: gt, lt
  Comparator #(.width(3)) comparator_18 (.a(Instruction[14:12]), .b(3'b011), .eq(comparator_18_eq));  // open: gt, lt
  Comparator #(.width(7)) comparator_19 (
    .a(Instruction[31:25]), .b(7'b0000001), .eq(comparator_19_eq));  // open: gt, lt
  Comparator #(.width(3)) comparator_20 (.a(Instruction[14:12]), .b(3'b000), .eq(comparator_20_eq));  // open: gt, lt
  Comparator #(.width(7)) comparator_21 (
    .a(Instruction[31:25]), .b(7'b0100000), .eq(comparator_21_eq));  // open: gt, lt
  // Probe on is_itype
  // Probe on is_rtype
  // Probe on is_add
  // Probe on is_and
  // Probe on is_or
  // Probe on is_xor
  // Probe on is_slt
  // Probe on is_sll
  and and_1 (is_sll, comparator_8_eq, comparator_9_eq);
  // Probe on is_srl
  and and_2 (is_srl, comparator_10_eq, comparator_11_eq);
  // Probe on is_sra
  and and_3 (is_sra, comparator_12_eq, comparator_13_eq);
  // Probe on is_mul
  and and_4 (is_mul, comparator_14_eq, comparator_15_eq);
  // Probe on is_mulh
  and and_5 (is_mulh, comparator_16_eq, comparator_17_eq);
  // Probe on is_mulhu
  and and_6 (is_mulhu, comparator_18_eq, comparator_19_eq);
  // Probe on is_sub
  and and_7 (is_sub, comparator_20_eq, comparator_21_eq);
  ROM #(.addrWidth(6), .dataWidth(16)) rom_1 (
    .addr(ROMInput), .data({rom_1_data, WBSel, MemWEn, ALUSel, BSel, ASel, BrUn, ImmSel, RegWEn}));
  // Probe on is_addi
  and and_8 (is_addi, is_itype, is_add);
  // Probe on is_andi
  and and_9 (is_andi, is_itype, is_and);
  // Probe on is_ori
  and and_10 (is_ori, is_itype, is_or);
  // Probe on is_xori
  and and_11 (is_xori, is_itype, is_xor);
  // Probe on is_slli
  and and_12 (is_slli, is_itype, is_sll);
  // Probe on is_srli
  and and_13 (is_srli, is_itype, is_srl);
  // Probe on is_srai
  and and_14 (is_srai, is_itype, is_sra);
  // Probe on is_slti
  and and_15 (is_slti, is_itype, is_slt);
  // Probe on is_add0
  and and_16 (is_add0, is_rtype, is_add);
  // Probe on is_and0
  and and_17 (is_and0, is_rtype, is_and);
  // Probe on is_or0
  and and_18 (is_or0, is_rtype, is_or);
  // Probe on is_xor0
  and and_19 (is_xor0, is_rtype, is_xor);
  // Probe on is_sll0
  and and_20 (is_sll0, is_rtype, is_sll);
  // Probe on is_srl0
  and and_21 (is_srl0, is_rtype, is_srl);
  // Probe on is_sra0
  and and_22 (is_sra0, is_rtype, is_sra);
  // Probe on is_slt0
  and and_23 (is_slt0, is_rtype, is_slt);
  // Probe on is_mul0
  and and_24 (is_mul0, is_rtype, is_mul);
  // Probe on is_mulh0
  and and_25 (is_mulh0, is_rtype, is_mulh);
  // Probe on is_mulhu0
  and and_26 (is_mulhu0, is_rtype, is_mulhu);
  // Probe on is_sub0
  and and_27 (is_sub0, is_rtype, is_sub);
  or or_1 (PCSel, BrEq, BrLt);
  Priority_Encoder #(.select_enc(6)) priority_encoder_1 (
    .in0(is_add0), .in1(is_mul0), .in2(is_sub0), .in3(is_sll0), .in4(is_mulh0), .in5(is_mulhu0),
    .in6(is_slt0), .in7(is_xor0), .in8(is_srl0), .in9(is_sra0), .in10(is_or0), .in11(is_and0),
    .in15(is_addi), .in16(is_slli), .in17(is_slti), .in18(is_xori), .in19(is_srli), .in20(is_srai),
    .in21(is_ori), .in22(is_andi), .out(ROMInput));  // open: in12, in13, in14, in23, in24, in25, in26, in27, in28, in29, in30, in31, in32, in33, in34, in35, in36, in37, in38, in39, in40, in41, in42, in43, in44, in45, in46, in47, in48, in49, in50, in51, in52, in53, in54, in55, in56, in57, in58, in59, in60, in61, in62, in63, gs, en_out, en_in
  // Probe on ROMInput

  // Other names for the same wires on the sheet: opcode[6:0] = Instruction[6:0]; funct3[2:0] = Instruction[14:12];
  //   funct7[6:0] = Instruction[31:25]

  // Notes on the sheet:
  //   INPUTS to your circuit
  //   contents of rom_1 (hex, n*v repeats v):
  //   1001 1401 1601 1081 1481 1581 1101 1201 1281 1681 1301 1381 0 0 0 1041 10c1 1141 1241 12c1 16c1 1341
  //   13c1
  //   ROM FOR CONTROL LOGIC
  //   DON'T CHANGE THE LOCATIONS OF THE INPUTS AND OUTPUTS!
  //   This is only if you choose to do the ROM option
  //   OUTPUT from your circuit
endmodule
